# Fritzing sketch part layout (saved by Fritzing 1.0.3b)
circuit board: 8.46667cm x 5.64444cm
breadboards: 2

parts:
  U1 = ESP32-38PinWide [part_number=ESP32-38PinWide]
  LCD1 = lcd-display3.5in-320x240-touch_1
  ZS-042_RTC1 = ZS-042 RTC Module
  Part1 = adafruit [part_number="Adafruit #5165"]
  S1 = Round Pushbutton
  S2 = Round Pushbutton
  S3 = Round Pushbutton
  VCC1 = 4 x AAA Battery Mount [internal_resistance=0.1Ω]
  S4 = SPST Switch [package=switch-spdt-smd]
  U2 = DIODE-ZENER [package=diode-zener]

nets (from the breadboard view):
  N1: U1.3.3, LCD1.connector0, LCD1.connector7, ZS-042_RTC1.VCC, Part1.connector11, Part1.connector16, Part1.connector58
  N2: U1.GPIO26, S1.leg0
  N3: U1.GPIO14, S2.leg0
  N4: U1.GPIO12, S3.leg0
  GND: U1.GND, LCD1.connector1, ZS-042_RTC1.GND, Part1.connector57, S1.leg1, S2.leg1, S3.leg1, VCC1.-
  N5: U1.VIN, U2.C
  N6: U1.GPIO15, LCD1.connector2
  N7: U1.GPIO2, LCD1.connector4
  N8: U1.GPIO4, LCD1.connector3
  N9: U1.GPIO5, LCD1.connector17
  N10: U1.GPIO18, LCD1.connector6, LCD1.connector14
  N11: U1.GPIO19, LCD1.connector8, LCD1.connector15
  N12: U1.GPIO21, ZS-042_RTC1.SDA, Part1.connector55
  N13: U1.GPIO22, ZS-042_RTC1.SCL, Part1.connector56
  N14: U1.GPIO23, LCD1.connector5, LCD1.connector16
  N15: VCC1.+, S4.P
  N16: S4.S, U2.A

notes:
  TFT display connections (left to right)
  3.3V red
  GND black
  CS green to ESP32 GPIO15
  RST white to ESP32 GPIO4
  DC/RS yellow to ESP32 GPIO2
  SDI blue to ESP32 GPIO23
  SCK yellow to ESP32 GPIO18
  3.3V red
  SDO white to ESP32 GPIO19
  SD card connections
  CS - green to ESP32 GPIO5
  SDI (MOSI) - blue to ESP32 GPIO23
  SDO (MISO) - white to ESP32 GPIO19
  SCK - yellow to ESP32 GPIO18
  I2C connections
  3.3V red
  GND black
  SCL yellow to ESP32 GPIO22
  SDA blue to ESP32 GPIO21
  user input buttons
  VBAT(6V) red to ESP32 5V
  GND black to common ground
  note diode to prevent reverse polarity connection

custom parts:
  ESP32-38PinWide: Generic 38-Pin ESP32 with wide format (only access to one side of pins on a breadboard) based on Stephen Lilley's HiLetgo ESP-WROOM-32 ESP32 ESP-32S Development Board.
